# Fritzing sketch 9Gservo_via_ESP8622_D1Mini (saved by Fritzing 0.9.4)

parts:
  WeMos_D1_Mini1 = WeMos D1 Mini
  M1 = Dagu DGServo 9g (Top view) [part_number=RS001B]

nets:
  5V: WeMos_D1_Mini1.5V, M1.vcc
  N1: WeMos_D1_Mini1.D4, M1.pulse
  N2: WeMos_D1_Mini1.G, M1.gnd
