# Fritzing sketch 9Gservo_via_PCA9685_D1Mini (saved by Fritzing 0.9.4)

parts:
  WeMos_D1_Mini1 = WeMos D1 Mini
  Part1 = Adafruit PCA9685 PWM/Servo Breakout [part_number=815]
  M2 = Dagu DGServo 9g (Top view) [part_number=RS001B]

nets:
  VCC: WeMos_D1_Mini1.5V, Part1.5.0V, Part1.VCC, M2.vcc
  N1: WeMos_D1_Mini1.D1, Part1.SCL
  GND: WeMos_D1_Mini1.G, Part1.GND, M2.gnd
  N2: WeMos_D1_Mini1.TX, Part1.SDA
  N3: Part1.PWM0, M2.pulse

custom parts:
  Adafruit PCA9685 PWM/Servo Breakout: Using only two pins, control 16 free-running PWM outputs! I2C-controlled PWM driver with a built in clock. Unlike the TLC5940 family, you do not need to continuously send it signal tying up your microcontroller, its completely free running! 5V compliant, which means you can control it from a 3.3V microcontroller and still safely drive up to 6V outputs (this is good for when you want to control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
